# Fritzing sketch RPi.MC (saved by Fritzing 0.9.2b)

parts:
  Raspberry_Pi_B_rev1 = Raspberry Pi B rev1
  S4 = Magnetic Door Switch [package=reed_switch_plastic]

nets:
  N1: Raspberry_Pi_B_rev1.3V3, S4.2
  N2: Raspberry_Pi_B_rev1.GPIO_17, S4.1
